// Logisim project AngelakosVirtual.circ as structural Verilog: 1 circuit, main circuit main
module main (
);

  wire and_1_out, and_2_out, and_4_out, and_5_out, and_6_out, and_7_out, and_8_out, and_9_out, and_10_out,
       and_11_out, and_12_out, and_13_out, and_14_out, and_15_out, and_16_out, clock_1_out, clock_2_out,
       clock_3_out, clock_4_out, comparator_1_eq, comparator_2_eq, comparator_3_eq, comparator_4_eq,
       comparator_5_eq, comparator_6_eq, comparator_7_gt, comparator_8_gt, comparator_9_eq, comparator_10_eq,
       decoder_1_out0, decoder_1_out1, decoder_1_out2, decoder_1_out3, decoder_1_out4, decoder_1_out5,
       decoder_1_out6, decoder_1_out7, nor_1_out, not_1_out, not_2_out, not_3_out, not_4_out, not_5_out,
       not_6_out, not_7_out, not_8_out, not_9_out, not_10_out, not_11_out, not_12_out, or_1_out, or_2_out,
       or_3_out, or_5_out, or_6_out, or_7_out, or_8_out, or_9_out, or_10_out, register_1_q;
  wire [1:0] controlME_EXME_q, controlME_IDEX_q;
  wire [2:0] controlWB_EXME_q, controlWB_IDEX_q, controlWB_MEWB_q;
  wire [3:0] action_IDEX_q, action_IFID_q, multiplexer_21_out, Register0_q, Register0_q_2, Register0_q_3,
       Register0_q_4, Register1_q, Register1_q_2, Register1_q_3, Register1_q_4, Register2_q, Register2_q_2,
       Register2_q_3, Register2_q_4, Register3_q, Register3_q_2, Register3_q_3, Register3_q_4, Register4_q,
       Register4_q_2, Register4_q_3, Register4_q_4, Register5_q, Register5_q_2, Register5_q_3, Register5_q_4,
       Register6_q, Register6_q_2, Register6_q_3, Register6_q_4, Register7_q, Register7_q_2, Register7_q_3,
       Register7_q_4;
  wire [4:0] controlEX_IDEX_q, multiplexer_9_out, multiplexer_10_out, multiplexer_12_out, multiplexer_14_out,
       multiplexer_20_out, Rd_IFID_q, Rm_IFID_q, Rn_IFID_q, Rt_IFID_q, WriteReg_EXME_q, WriteReg_IDEX_q,
       WriteReg_MEWB_q;
  wire [9:0] imm_IDEX_q;
  wire [10:0] imm_IFID_q, multiplexer_16_out, multiplexer_17_out, multiplexer_20_out_3, opcode_IFID_q;
  wire [10:10] imm_IDEX_q_2;
  wire [15:0] adder_1_out, adder_2_out, adder_3_out, ALUout_MEWB_q, ALUout_q, and_3_out, bit_extender_1_out,
       bit_extender_2_out, divider_1_out, multiplexer_1_out, multiplexer_2_out, multiplexer_3_out,
       multiplexer_4_out, multiplexer_5_out, multiplexer_6_out, multiplexer_7_out, multiplexer_8_out,
       multiplexer_11_out, multiplexer_13_out, multiplexer_15_out, multiplexer_18_out, multiplexer_19_out,
       multiplier_1_out, nextPC_EXME_q, nextPC_IDEX_q, nextPC_IFID_q, nextPC_MEWB_q, or_4_out, PC_IDEX_q,
       PC_IFID_q, PC_q, ram_1_dout, ReadDataM_q, RegData1_q, RegData2_EXME_q, RegData2_IDEX_q,
       subtractor_1_out, subtractor_2_out;
  wire [35:0] ram_2_dout, register_2_q, register_3_q, register_4_q;
  wire [35:5] multiplexer_20_out_2;

  Register #(.width(16)) nextPC_IDEX (
    .D(multiplexer_1_out), .en(1'b1), .clk(clock_3_out), .Q(nextPC_IDEX_q));  // open: clr
  Register #(.width(16)) Register0 (
    .D(multiplexer_19_out), .en(and_9_out), .clk(clock_2_out),
    .Q({Register0_q_4, Register0_q_3, Register0_q_2, Register0_q}));  // open: clr
  Register #(.width(16)) Register1 (
    .D(multiplexer_19_out), .en(and_10_out), .clk(clock_2_out),
    .Q({Register1_q_4, Register1_q_3, Register1_q_2, Register1_q}));  // open: clr
  Register #(.width(16)) Register2 (
    .D(multiplexer_19_out), .en(and_11_out), .clk(clock_2_out),
    .Q({Register2_q_4, Register2_q_3, Register2_q_2, Register2_q}));  // open: clr
  Register #(.width(16)) Register3 (
    .D(multiplexer_19_out), .en(and_12_out), .clk(clock_2_out),
    .Q({Register3_q_4, Register3_q_3, Register3_q_2, Register3_q}));  // open: clr
  Register #(.width(16)) Register4 (
    .D(multiplexer_19_out), .en(and_13_out), .clk(clock_2_out),
    .Q({Register4_q_4, Register4_q_3, Register4_q_2, Register4_q}));  // open: clr
  Register #(.width(16)) Register5 (
    .D(multiplexer_19_out), .en(and_14_out), .clk(clock_2_out),
    .Q({Register5_q_4, Register5_q_3, Register5_q_2, Register5_q}));  // open: clr
  Register #(.width(16)) Register6 (
    .D(multiplexer_19_out), .en(and_15_out), .clk(clock_2_out),
    .Q({Register6_q_4, Register6_q_3, Register6_q_2, Register6_q}));  // open: clr
  Register #(.width(16)) Register7 (
    .D(multiplexer_19_out), .en(and_16_out), .clk(clock_2_out),
    .Q({Register7_q_4, Register7_q_3, Register7_q_2, Register7_q}));  // open: clr
  Multiplexer #(.width(16)) multiplexer_1 (
    .in0(nextPC_IFID_q), .in1({16{1'b0}}), .out(multiplexer_1_out), .sel(and_8_out));
  Register #(.width(16)) nextPC_EXME (.D(nextPC_IDEX_q), .en(1'b1), .clk(clock_3_out), .Q(nextPC_EXME_q));  // open: clr
  Multiplexer #(.width(16)) multiplexer_2 (.in0(PC_IFID_q), .in1({16{1'b0}}), .out(multiplexer_2_out), .sel(and_8_out));
  Adder #(.width(16)) adder_1 (.a(bit_extender_1_out), .b(PC_IDEX_q), .out(adder_1_out));  // open: cin, cout
  Subtractor #(.width(16)) subtractor_1 (
    .a(PC_IDEX_q), .b(bit_extender_1_out), .out(subtractor_1_out));  // open: bin, bout
  Register #(.width(16)) nextPC_MEWB (.D(nextPC_EXME_q), .en(1'b1), .clk(clock_3_out), .Q(nextPC_MEWB_q));  // open: clr
  Register #(.width(16)) PC_IDEX (.D(multiplexer_2_out), .en(1'b1), .clk(clock_3_out), .Q(PC_IDEX_q));  // open: clr
  Multiplexer #(.width(16)) multiplexer_3 (
    .in0(adder_1_out), .in1(subtractor_1_out), .out(multiplexer_3_out), .sel(imm_IDEX_q_2[10]));
  Comparator #(.width(16)) comparator_1 (.a(multiplexer_6_out), .b(PC_q), .eq(comparator_1_eq));  // open: gt, lt
  Adder #(.width(16)) adder_2 (.a(PC_q), .b(16'h1), .out(adder_2_out));  // open: cin, cout
  Register #(.width(16)) nextPC_IFID (
    .D(adder_2_out), .en(not_1_out), .clk(clock_3_out), .Q(nextPC_IFID_q));  // open: clr
  not not_1 (not_1_out, and_8_out);
  Register #(.width(2)) controlME_EXME (
    .D(controlME_IDEX_q), .en(1'b1), .clk(clock_3_out), .Q(controlME_EXME_q));  // open: clr
  Register #(.width(5)) controlEX_IDEX (
    .D(multiplexer_16_out[10:6]), .en(1'b1), .clk(clock_3_out), .Q(controlEX_IDEX_q));  // open: clr
  assign bit_extender_1_out = {{6{1'b0}}, imm_IDEX_q};  // Bit_Extender bit_extender_1
  or or_1 (or_1_out, controlEX_IDEX_q[4], controlEX_IDEX_q[3], controlEX_IDEX_q[2]);
  Multiplexer #(.width(16)) multiplexer_4 (
    .in0(multiplexer_7_out), .in1(multiplexer_6_out), .out(multiplexer_4_out), .sel(and_2_out));
  not not_2 (not_2_out, comparator_1_eq);
  Register #(.width(16)) PC_IFID (.D(PC_q), .en(not_3_out), .clk(clock_3_out), .Q(PC_IFID_q));  // open: clr
  not not_3 (not_3_out, and_8_out);
  and and_1 (and_1_out, controlEX_IDEX_q[3], register_1_q);
  or or_2 (or_2_out, and_1_out, controlEX_IDEX_q[2]);
  Multiplexer #(.width(16)) multiplexer_5 (
    .in0(nextPC_IDEX_q), .in1(multiplexer_3_out), .out(multiplexer_5_out), .sel(or_2_out));
  Multiplexer #(.width(16)) multiplexer_6 (
    .in0(multiplexer_5_out), .in1(multiplexer_13_out), .out(multiplexer_6_out), .sel(controlEX_IDEX_q[4]));
  Register #(.width(3)) controlWB_EXME (
    .D(controlWB_IDEX_q), .en(1'b1), .clk(clock_3_out), .Q(controlWB_EXME_q));  // open: clr
  and and_2 (and_2_out, not_2_out, or_1_out);
  Register #(.width(2)) controlME_IDEX (
    .D(multiplexer_16_out[5:4]), .en(1'b1), .clk(clock_3_out), .Q(controlME_IDEX_q));  // open: clr
  Register #(.width(3)) controlWB_MEWB (
    .D(controlWB_EXME_q), .en(1'b1), .clk(clock_3_out), .Q(controlWB_MEWB_q));  // open: clr
  Multiplexer #(.width(16)) multiplexer_7 (.in0(adder_2_out), .in1(PC_q), .out(multiplexer_7_out), .sel(and_8_out));
  or or_3 (or_3_out, multiplexer_16_out[10], multiplexer_16_out[9], multiplexer_16_out[8]);
  not not_4 (not_4_out, and_8_out);
  Register #(.width(5)) Rn_IFID (
    .D(multiplexer_20_out_2[9:5]), .en(not_4_out), .clk(clock_3_out), .Q(Rn_IFID_q));  // open: clr
  Multiplexer #(.select(5), .width(16)) multiplexer_8 (
    .in0({Register0_q_4, Register0_q_3, Register0_q_2, Register0_q}),
    .in1({Register1_q_4, Register1_q_3, Register1_q_2, Register1_q}),
    .in2({Register2_q_4, Register2_q_3, Register2_q_2, Register2_q}),
    .in3({Register3_q_4, Register3_q_3, Register3_q_2, Register3_q}),
    .in4({Register4_q_4, Register4_q_3, Register4_q_2, Register4_q}),
    .in5({Register5_q_4, Register5_q_3, Register5_q_2, Register5_q}),
    .in6({Register6_q_4, Register6_q_3, Register6_q_2, Register6_q}),
    .in7({Register7_q_4, Register7_q_3, Register7_q_2, Register7_q}), .out(multiplexer_8_out),
    .sel(multiplexer_9_out));  // open: in8, in9, in10, in11, in12, in13, in14, in15, in16, in17, in18, in19, in20, in21, in22, in23, in24, in25, in26, in27, in28, in29, in30, in31
  Register #(.width(3)) controlWB_IDEX (
    .D(multiplexer_16_out[3:1]), .en(1'b1), .clk(clock_3_out), .Q(controlWB_IDEX_q));  // open: clr
  not not_5 (not_5_out, and_8_out);
  Multiplexer #(.width(5)) multiplexer_9 (.in0(Rn_IFID_q), .in1({5{1'b0}}), .out(multiplexer_9_out), .sel(and_8_out));
  Register #(.width(1)) register_1 (
    .D(comparator_2_eq), .en(controlEX_IDEX_q[1]), .clk(clock_1_out), .Q(register_1_q));  // open: clr
  Clock clock_1 (.out(clock_1_out));
  Register #(.width(5)) Rm_IFID (
    .D(multiplexer_20_out_2[20:16]), .en(not_5_out), .clk(clock_3_out), .Q(Rm_IFID_q));  // open: clr
  assign and_3_out = RegData1_q & multiplexer_15_out;  // AND_Gate and_3, 16 bits wide
  Clock clock_2 (.out(clock_2_out));
  Clock #(.highDuration(2)) clock_3 (.out(clock_3_out));
  Multiplexer #(.width(5)) multiplexer_10 (
    .in0(Rt_IFID_q), .in1(Rm_IFID_q), .out(multiplexer_10_out), .sel(multiplexer_16_out[0]));
  Multiplexer #(.select(5), .width(16)) multiplexer_11 (
    .in0({Register0_q_4, Register0_q_3, Register0_q_2, Register0_q}),
    .in1({Register1_q_4, Register1_q_3, Register1_q_2, Register1_q}),
    .in2({Register2_q_4, Register2_q_3, Register2_q_2, Register2_q}),
    .in3({Register3_q_4, Register3_q_3, Register3_q_2, Register3_q}),
    .in4({Register4_q_4, Register4_q_3, Register4_q_2, Register4_q}),
    .in5({Register5_q_4, Register5_q_3, Register5_q_2, Register5_q}),
    .in6({Register6_q_4, Register6_q_3, Register6_q_2, Register6_q}),
    .in7({Register7_q_4, Register7_q_3, Register7_q_2, Register7_q}), .out(multiplexer_11_out),
    .sel(multiplexer_12_out));  // open: in8, in9, in10, in11, in12, in13, in14, in15, in16, in17, in18, in19, in20, in21, in22, in23, in24, in25, in26, in27, in28, in29, in30, in31
  Register #(.width(5)) Rt_IFID (
    .D(multiplexer_20_out), .en(not_6_out), .clk(clock_3_out), .Q(Rt_IFID_q));  // open: clr
  not not_6 (not_6_out, and_8_out);
  Multiplexer #(.width(5)) multiplexer_12 (
    .in0(multiplexer_10_out), .in1({5{1'b0}}), .out(multiplexer_12_out), .sel(and_8_out));
  Register #(.width(16)) RegData1 (.D(multiplexer_8_out), .en(1'b1), .clk(clock_3_out), .Q(RegData1_q));  // open: clr
  assign or_4_out = RegData1_q | multiplexer_15_out;  // OR_Gate or_4, 16 bits wide
  Multiplexer #(.select(4), .width(16)) multiplexer_13 (
    .in0(and_3_out), .in1(or_4_out), .in2(adder_3_out), .in3(subtractor_2_out), .in4(multiplier_1_out),
    .in5(divider_1_out), .in7(multiplexer_15_out), .in8(and_3_out), .in9(or_4_out), .in10(adder_3_out),
    .in11(subtractor_2_out), .out(multiplexer_13_out), .sel(action_IDEX_q));  // open: in6, in12, in13, in14, in15
  Comparator #(.width(16)) comparator_2 (.a(multiplexer_13_out), .b({16{1'b0}}), .eq(comparator_2_eq));  // open: gt, lt
  Register #(.width(16)) PC (.D(multiplexer_4_out), .en(or_5_out), .clk(clock_3_out), .Q(PC_q));  // open: clr
  nor nor_1 (nor_1_out, or_10_out, or_3_out);
  or or_5 (or_5_out, nor_1_out, or_1_out);
  Register #(.width(5)) Rd_IFID (
    .D(multiplexer_20_out), .en(not_7_out), .clk(clock_3_out), .Q(Rd_IFID_q));  // open: clr
  not not_7 (not_7_out, and_8_out);
  Register #(.width(36)) register_2 (
    .D({multiplexer_20_out_2[35:32], multiplexer_20_out_3, multiplexer_20_out_2[20:5], multiplexer_20_out}),
    .en(not_8_out), .clk(clock_3_out), .Q(register_2_q));  // open: clr
  not not_8 (not_8_out, and_8_out);
  Register #(.width(36)) register_3 (.D(register_2_q), .en(1'b1), .clk(clock_3_out), .Q(register_3_q));  // open: clr
  Register #(.width(36)) register_4 (.D(register_3_q), .en(1'b1), .clk(clock_3_out), .Q(register_4_q));  // open: clr
  Register #(.width(16)) RegData2_IDEX (
    .D(multiplexer_11_out), .en(1'b1), .clk(clock_3_out), .Q(RegData2_IDEX_q));  // open: clr
  Subtractor #(.width(16)) subtractor_2 (
    .a(RegData1_q), .b(multiplexer_15_out), .out(subtractor_2_out));  // open: bin, bout
  Multiplexer #(.width(5)) multiplexer_14 (.in0(Rd_IFID_q), .in1({5{1'b0}}), .out(multiplexer_14_out), .sel(and_8_out));
  Multiplexer #(.width(16)) multiplexer_15 (
    .in0(RegData2_IDEX_q), .in1(bit_extender_2_out), .out(multiplexer_15_out), .sel(controlEX_IDEX_q[0]));
  Adder #(.width(16)) adder_3 (.a(RegData1_q), .b(multiplexer_15_out), .out(adder_3_out));  // open: cin, cout
  Register #(.width(16)) ALUout (.D(multiplexer_13_out), .en(1'b1), .clk(clock_3_out), .Q(ALUout_q));  // open: clr
  Register #(.width(11)) imm_IFID (
    .D(multiplexer_20_out_2[20:10]), .en(not_9_out), .clk(clock_3_out), .Q(imm_IFID_q));  // open: clr
  not not_9 (not_9_out, and_8_out);
  Register #(.width(5)) WriteReg_IDEX (
    .D(multiplexer_14_out), .en(1'b1), .clk(clock_3_out), .Q(WriteReg_IDEX_q));  // open: clr
  Multiplier #(.mode("twosComplement"), .width(16)) multiplier_1 (
    .a(RegData1_q), .b(multiplexer_15_out), .out(multiplier_1_out));  // open: cin, cout
  Clock clock_4 (.out(clock_4_out));
  assign bit_extender_2_out = {{5{imm_IDEX_q_2[10]}}, {imm_IDEX_q_2[10], imm_IDEX_q}};  // Bit_Extender bit_extender_2
  Divider #(.mode("twosComplement"), .width(16)) divider_1 (
    .a(RegData1_q), .b(multiplexer_15_out), .out(divider_1_out));  // open: upper, rem
  Register #(.width(11)) opcode_IFID (
    .D(multiplexer_20_out_3), .en(not_10_out), .clk(clock_3_out), .Q(opcode_IFID_q));  // open: clr
  not not_10 (not_10_out, and_8_out);
  Multiplexer #(.width(11)) multiplexer_16 (
    .in0(opcode_IFID_q), .in1({11{1'b0}}), .out(multiplexer_16_out), .sel(and_8_out));
  Comparator #(.width(5)) comparator_3 (.a(Rn_IFID_q), .b(WriteReg_IDEX_q), .eq(comparator_3_eq));  // open: gt, lt
  Comparator #(.width(5)) comparator_4 (
    .a(multiplexer_10_out), .b(WriteReg_IDEX_q), .eq(comparator_4_eq));  // open: gt, lt
  Comparator #(.width(5)) comparator_5 (.a(Rn_IFID_q), .b(WriteReg_EXME_q), .eq(comparator_5_eq));  // open: gt, lt
  Comparator #(.width(5)) comparator_6 (
    .a(multiplexer_10_out), .b(WriteReg_EXME_q), .eq(comparator_6_eq));  // open: gt, lt
  Comparator #(.width(36)) comparator_7 (.a(register_3_q), .b({36{1'b0}}), .gt(comparator_7_gt));  // open: eq, lt
  Comparator #(.width(36)) comparator_8 (.a(register_4_q), .b(36'h1), .gt(comparator_8_gt));  // open: eq, lt
  Multiplexer #(.width(11)) multiplexer_17 (
    .in0(imm_IFID_q), .in1({11{1'b0}}), .out(multiplexer_17_out), .sel(and_8_out));
  Register #(.width(11)) imm_IDEX (
    .D(multiplexer_17_out), .en(1'b1), .clk(clock_3_out), .Q({imm_IDEX_q_2[10], imm_IDEX_q}));  // open: clr
  Register #(.width(16)) RegData2_EXME (
    .D(RegData2_IDEX_q), .en(1'b1), .clk(clock_3_out), .Q(RegData2_EXME_q));  // open: clr
  RAM #(.addrWidth(16), .dataWidth(16), .enables("line")) ram_1 (
    .addr(ALUout_q), .we(controlME_EXME_q[1]), .oe(controlME_EXME_q[0]), .clk(clock_4_out),
    .din(RegData2_EXME_q), .dout(ram_1_dout));
  Register #(.width(16)) ReadDataM (.D(ram_1_dout), .en(1'b1), .clk(clock_3_out), .Q(ReadDataM_q));  // open: clr
  Multiplexer #(.width(16)) multiplexer_18 (
    .in0(ALUout_MEWB_q), .in1(ReadDataM_q), .out(multiplexer_18_out), .sel(controlWB_MEWB_q[0]));
  Multiplexer #(.width(16)) multiplexer_19 (
    .in0(multiplexer_18_out), .in1(nextPC_MEWB_q), .out(multiplexer_19_out), .sel(controlWB_MEWB_q[1]));
  Multiplexer #(.width(36)) multiplexer_20 (
    .in0(ram_2_dout), .in1({36{1'b0}}),
    .out({multiplexer_20_out_2[35:32], multiplexer_20_out_3, multiplexer_20_out_2[20:5], multiplexer_20_out}),
    .sel(or_7_out));
  Comparator #(.width(6)) comparator_9 (
    .a(multiplexer_20_out_2[15:10]), .b(6'b111000), .eq(comparator_9_eq));  // open: gt, lt
  or or_6 (or_6_out, comparator_3_eq, and_4_out);
  and and_4 (and_4_out, comparator_9_eq, comparator_4_eq);
  and and_5 (and_5_out, comparator_9_eq, comparator_6_eq);
  Comparator #(.width(4)) comparator_10 (.a(action_IFID_q), .b(4'b0111), .eq(comparator_10_eq));  // open: gt, lt
  or or_7 (or_7_out, or_3_out, or_1_out);
  Register #(.width(4)) action_IFID (
    .D(multiplexer_20_out_2[35:32]), .en(not_11_out), .clk(clock_3_out), .Q(action_IFID_q));  // open: clr
  not not_11 (not_11_out, and_8_out);
  and and_6 (and_6_out, or_6_out, comparator_7_gt);
  and and_7 (and_7_out, or_8_out, comparator_8_gt);
  or or_8 (or_8_out, comparator_5_eq, and_5_out);
  Multiplexer #(.width(4)) multiplexer_21 (
    .in0(action_IFID_q), .in1(4'b0000), .out(multiplexer_21_out), .sel(and_8_out));
  Register #(.width(16)) ALUout_MEWB (.D(ALUout_q), .en(1'b1), .clk(clock_3_out), .Q(ALUout_MEWB_q));  // open: clr
  or or_9 (or_9_out, and_6_out, and_7_out);
  not not_12 (not_12_out, comparator_10_eq);
  Register #(.width(4)) action_IDEX (
    .D(multiplexer_21_out), .en(1'b1), .clk(clock_3_out), .Q(action_IDEX_q));  // open: clr
  or or_10 (or_10_out, multiplexer_20_out_3[10], multiplexer_20_out_3[9], multiplexer_20_out_3[8]);
  and and_8 (and_8_out, or_9_out, not_12_out);
  Register #(.width(5)) WriteReg_EXME (
    .D(WriteReg_IDEX_q), .en(1'b1), .clk(clock_3_out), .Q(WriteReg_EXME_q));  // open: clr
  Register #(.width(5)) WriteReg_MEWB (
    .D(WriteReg_EXME_q), .en(1'b1), .clk(clock_3_out), .Q(WriteReg_MEWB_q));  // open: clr
  Decoder #(.select(5)) decoder_1 (
    .out0(decoder_1_out0), .out1(decoder_1_out1), .out2(decoder_1_out2), .out3(decoder_1_out3),
    .out4(decoder_1_out4), .out5(decoder_1_out5), .out6(decoder_1_out6), .out7(decoder_1_out7),
    .sel(WriteReg_MEWB_q));  // open: out8, out9, out10, out11, out12, out13, out14, out15, out16, out17, out18, out19, out20, out21, out22, out23, out24, out25, out26, out27, out28, out29, out30, out31, en
  RAM #(.addrWidth(16), .dataWidth(36), .enables("line")) ram_2 (
    .addr(PC_q), .we(1'b0), .clk(clock_3_out), .dout(ram_2_dout));  // open: din
  and and_9 (and_9_out, decoder_1_out0, controlWB_MEWB_q[2]);
  and and_10 (and_10_out, decoder_1_out1, controlWB_MEWB_q[2]);
  and and_11 (and_11_out, decoder_1_out2, controlWB_MEWB_q[2]);
  and and_12 (and_12_out, decoder_1_out3, controlWB_MEWB_q[2]);
  and and_13 (and_13_out, decoder_1_out4, controlWB_MEWB_q[2]);
  and and_14 (and_14_out, decoder_1_out5, controlWB_MEWB_q[2]);
  and and_15 (and_15_out, decoder_1_out6, controlWB_MEWB_q[2]);
  and and_16 (and_16_out, decoder_1_out7, controlWB_MEWB_q[2]);
  Hex_Digit_Display hex_digit_display_1 (.value(Register0_q_4));  // open: dp
  Hex_Digit_Display hex_digit_display_2 (.value(Register1_q_4));  // open: dp
  Hex_Digit_Display hex_digit_display_3 (.value(Register2_q_4));  // open: dp
  Hex_Digit_Display hex_digit_display_4 (.value(Register3_q_4));  // open: dp
  Hex_Digit_Display hex_digit_display_5 (.value(Register4_q_4));  // open: dp
  Hex_Digit_Display hex_digit_display_6 (.value(Register5_q_4));  // open: dp
  Hex_Digit_Display hex_digit_display_7 (.value(Register6_q_4));  // open: dp
  Hex_Digit_Display hex_digit_display_8 (.value(Register7_q_4));  // open: dp
  Hex_Digit_Display hex_digit_display_9 (.value(Register0_q_3));  // open: dp
  Hex_Digit_Display hex_digit_display_10 (.value(Register0_q_2));  // open: dp
  Hex_Digit_Display hex_digit_display_11 (.value(Register1_q_3));  // open: dp
  Hex_Digit_Display hex_digit_display_12 (.value(Register1_q_2));  // open: dp
  Hex_Digit_Display hex_digit_display_13 (.value(Register2_q_3));  // open: dp
  Hex_Digit_Display hex_digit_display_14 (.value(Register2_q_2));  // open: dp
  Hex_Digit_Display hex_digit_display_15 (.value(Register3_q_3));  // open: dp
  Hex_Digit_Display hex_digit_display_16 (.value(Register3_q_2));  // open: dp
  Hex_Digit_Display hex_digit_display_17 (.value(Register4_q_3));  // open: dp
  Hex_Digit_Display hex_digit_display_18 (.value(Register4_q_2));  // open: dp
  Hex_Digit_Display hex_digit_display_19 (.value(Register5_q_3));  // open: dp
  Hex_Digit_Display hex_digit_display_20 (.value(Register5_q_2));  // open: dp
  Hex_Digit_Display hex_digit_display_21 (.value(Register6_q_3));  // open: dp
  Hex_Digit_Display hex_digit_display_22 (.value(Register6_q_2));  // open: dp
  Hex_Digit_Display hex_digit_display_23 (.value(Register7_q_3));  // open: dp
  Hex_Digit_Display hex_digit_display_24 (.value(Register7_q_2));  // open: dp
  Hex_Digit_Display hex_digit_display_25 (.value(Register0_q));  // open: dp
  Hex_Digit_Display hex_digit_display_26 (.value(Register1_q));  // open: dp
  Hex_Digit_Display hex_digit_display_27 (.value(Register2_q));  // open: dp
  Hex_Digit_Display hex_digit_display_28 (.value(Register3_q));  // open: dp
  Hex_Digit_Display hex_digit_display_29 (.value(Register4_q));  // open: dp
  Hex_Digit_Display hex_digit_display_30 (.value(Register5_q));  // open: dp
  Hex_Digit_Display hex_digit_display_31 (.value(Register6_q));  // open: dp
  Hex_Digit_Display hex_digit_display_32 (.value(Register7_q));  // open: dp

  // Notes on the sheet:
  //   The Virtual CPU
  //   Register 0
  //   Register 1
  //   Register 2
  //   Register 3
  //   Register 4
  //   Register 5
  //   Register 6
  //   Names: Matthew Angelakos and Elliot Neimann
  //   I pledge my honor that I have abided by the Stevens Honor System
  //   Register 7 (Link Register)
endmodule
